// Logisim project PandesalCPU.circ as structural Verilog: 18 circuits, main circuit PandesalCPU
module PandesalCPU (
  input  Reset
);

  wire ABL_cout, and_1_out, and_2_out, and_3_out, and_4_out, and_5_out, and_6_out, clock_1_out,
       decoder_1_out0, decoder_1_out1, decoder_1_out2, decoder_1_out3, decoder_1_out4, decoder_1_out5,
       decoder_1_out6, decoder_1_out7, decoder_1_out8, decoder_1_out9, decoder_1_out10, decoder_1_out11,
       decoder_1_out12, decoder_1_out13, decoder_1_out14, decoder_1_out15, decoder_2_out0, decoder_2_out1,
       decoder_2_out2, decoder_2_out3, decoder_2_out4, decoder_2_out5, decoder_2_out6, decoder_2_out7,
       decoder_2_out8, decoder_2_out9, decoder_2_out10, decoder_2_out11, decoder_2_out12, decoder_2_out13,
       decoder_2_out14, decoder_2_out15, decoder_3_out1, decoder_3_out2, decoder_3_out3,
       demultiplexer_1_out0, demultiplexer_1_out1, demultiplexer_2_out0, demultiplexer_2_out1,
       demultiplexer_3_out0, demultiplexer_3_out1, multiplexer_1_out, multiplexer_2_out, not_1_out,
       not_2_out, not_3_out, not_4_out, not_5_out, not_6_out, not_7_out, or_1_out, PCL_c;
  wire [0:0] Microcode_data_2;
  wire [1:0] multiplexer_3_out;
  wire [3:0] ALU_n, multiplexer_4_out, S, SC;
  wire [7:0] A, ABH, ABL, ALU_y, B, GP0, GP1, GP2, GP3, GP4, Instruction_Register_q, IR, multiplexer_5_out,
       multiplexer_6_out, O, PCH, PCL, rom_1_data, SP, X, Y;
  wire [15:1] Microcode_data;

  Clock clock_1 (.out(clock_1_out));
  ROM #(.addrWidth(12), .dataWidth(16)) Microcode (.addr({IR, SC}), .data({Microcode_data, Microcode_data_2[0]}));
  Register8 Instruction_Register (
    .D(Instruction_Register_q), .Load(decoder_1_out2), .Enable(decoder_2_out2), .Clk(clock_1_out),
    .Reset(Reset), .Q(Instruction_Register_q), .AlwaysQ(IR));
  and and_1 (and_1_out, ABH[7], not_1_out);
  and and_2 (and_2_out, and_1_out, decoder_1_out15);
  not not_1 (not_1_out, ABH[6]);
  // RGB_Video #(.cursor("No Cursor"), .scale(4)) rgb_video_1: pin names not known; wires that end beside it: Reset, clock_1_out, and_2_out, ABL[6:0], {ABH[5:0], ABL[7]}, Instruction_Register_q
  Increment4 StepCounter (.Reset(or_1_out), .Clk(clock_1_out), .O(SC));
  Multiplexer multiplexer_1 (.in0(1'b0), .in1(multiplexer_2_out), .out(multiplexer_1_out), .sel(decoder_3_out2));
  not not_2 (not_2_out, S[3]);
  not not_3 (not_3_out, S[2]);
  not not_4 (not_4_out, S[0]);
  Multiplexer #(.select(3)) multiplexer_2 (
    .in0(S[3]), .in1(not_2_out), .in2(not_3_out), .in3(not_4_out), .in4(S[2]), .in5(S[0]), .in6(S[1]),
    .in7(not_5_out), .out(multiplexer_2_out));  // open: sel
  not not_5 (not_5_out, S[1]);
  and and_3 (and_3_out, decoder_1_out15, not_6_out);
  not not_6 (not_6_out, ABH[7]);
  and and_4 (and_4_out, not_6_out, decoder_2_out15);
  or or_1 (or_1_out, Reset, multiplexer_1_out, decoder_3_out1);
  Demultiplexer demultiplexer_1 (
    .out0(demultiplexer_1_out0), .out1(demultiplexer_1_out1), .in(decoder_2_out0), .sel(Microcode_data[3]));
  Decoder #(.enable("false"), .select(4)) decoder_1 (
    .out0(decoder_1_out0), .out1(decoder_1_out1), .out2(decoder_1_out2), .out3(decoder_1_out3),
    .out4(decoder_1_out4), .out5(decoder_1_out5), .out6(decoder_1_out6), .out7(decoder_1_out7),
    .out8(decoder_1_out8), .out9(decoder_1_out9), .out10(decoder_1_out10), .out11(decoder_1_out11),
    .out12(decoder_1_out12), .out13(decoder_1_out13), .out14(decoder_1_out14), .out15(decoder_1_out15),
    .sel(Microcode_data[11:8]));
  Decoder #(.enable("false"), .select(4)) decoder_2 (
    .out0(decoder_2_out0), .out1(decoder_2_out1), .out2(decoder_2_out2), .out3(decoder_2_out3),
    .out4(decoder_2_out4), .out5(decoder_2_out5), .out6(decoder_2_out6), .out7(decoder_2_out7),
    .out8(decoder_2_out8), .out9(decoder_2_out9), .out10(decoder_2_out10), .out11(decoder_2_out11),
    .out12(decoder_2_out12), .out13(decoder_2_out13), .out14(decoder_2_out14), .out15(decoder_2_out15),
    .sel(Microcode_data[15:12]));
  Decoder #(.enable("false"), .select(2)) decoder_3 (
    .out1(decoder_3_out1), .out2(decoder_3_out2), .out3(decoder_3_out3), .sel(Microcode_data[2:1]));  // open: out0
  RAM #(.addrWidth(15), .databus("bidir"), .enables("line"), .trigger("high"), .\type ("nonvolatile")) ram_1 (
    .addr({ABH[6:0], ABL}), .we(and_3_out), .oe(and_4_out), .clk(not_7_out), .data(Instruction_Register_q));
  not not_7 (not_7_out, ABH[7]);
  Multiplexer #(.width(2)) multiplexer_3 (
    .in0({1'b0, Microcode_data_2[0]}), .in1(2'b10), .out(multiplexer_3_out), .sel(decoder_3_out2));
  Demultiplexer demultiplexer_2 (
    .out0(demultiplexer_2_out0), .out1(demultiplexer_2_out1), .in(decoder_1_out0), .sel(Microcode_data[3]));
  Demultiplexer demultiplexer_3 (
    .out0(demultiplexer_3_out0), .out1(demultiplexer_3_out1), .in(decoder_1_out1), .sel(Microcode_data[3]));
  assign Instruction_Register_q[0] = decoder_2_out1 ? decoder_2_out1 : 1'bz;  // Controlled_Buffer controlled_buffer_1
  assign Instruction_Register_q[1] = decoder_2_out1 ? 1'b0 : 1'bz;  // Controlled_Buffer controlled_buffer_2
  assign Instruction_Register_q[2] = decoder_2_out1 ? 1'b0 : 1'bz;  // Controlled_Buffer controlled_buffer_3
  assign Instruction_Register_q[3] = decoder_2_out1 ? 1'b0 : 1'bz;  // Controlled_Buffer controlled_buffer_4
  assign Instruction_Register_q[4] = decoder_2_out1 ? 1'b0 : 1'bz;  // Controlled_Buffer controlled_buffer_5
  assign Instruction_Register_q[5] = decoder_2_out1 ? 1'b0 : 1'bz;  // Controlled_Buffer controlled_buffer_6
  assign Instruction_Register_q[6] = decoder_2_out1 ? 1'b0 : 1'bz;  // Controlled_Buffer controlled_buffer_7
  assign Instruction_Register_q[7] = decoder_2_out1 ? 1'b0 : 1'bz;  // Controlled_Buffer controlled_buffer_8
  Hex_Digit_Display #(.decimalPoint("false")) hex_digit_display_1 (.value(PCH[7:4]));
  Hex_Digit_Display #(.decimalPoint("false")) hex_digit_display_2 (.value(PCH[3:0]));
  _7_Segment_Display #(.decimalPoint("false")) u_7_segment_display_1 (.b(S[3]), .c(S[3]));  // open: g, f, a, e, d
  _7_Segment_Display #(.decimalPoint("false")) u_7_segment_display_2 (.b(S[2]), .c(S[2]));  // open: g, f, a, e, d
  Hex_Digit_Display #(.decimalPoint("false")) hex_digit_display_3 (.value(X[7:4]));
  Hex_Digit_Display #(.decimalPoint("false")) hex_digit_display_4 (.value(GP2[7:4]));
  Hex_Digit_Display #(.decimalPoint("false")) hex_digit_display_5 (.value(PCL[7:4]));
  Hex_Digit_Display #(.decimalPoint("false")) hex_digit_display_6 (.value(PCL[3:0]));
  _7_Segment_Display #(.decimalPoint("false")) u_7_segment_display_3 (.b(S[1]), .c(S[1]));  // open: g, f, a, e, d
  _7_Segment_Display #(.decimalPoint("false")) u_7_segment_display_4 (.b(S[0]), .c(S[0]));  // open: g, f, a, e, d
  Hex_Digit_Display #(.decimalPoint("false")) hex_digit_display_7 (.value(X[3:0]));
  Hex_Digit_Display #(.decimalPoint("false")) hex_digit_display_8 (.value(GP2[3:0]));
  Hex_Digit_Display #(.decimalPoint("false")) hex_digit_display_9 (.value(ABH[7:4]));
  ProgramCounter u_PCL (
    .Cin(1'b0), .Inc(multiplexer_3_out), .Load(demultiplexer_2_out0), .Reset(Reset), .Clk(clock_1_out),
    .Address(Instruction_Register_q), .Enable(demultiplexer_1_out0), .C(PCL_c), .PC(Instruction_Register_q),
    .AlwaysQ(PCL));
  ProgramCounter u_PCH (
    .Cin(PCL_c), .Inc(2'b00), .Load(demultiplexer_2_out1), .Reset(Reset), .Clk(clock_1_out),
    .Address(Instruction_Register_q), .Enable(demultiplexer_1_out1), .PC(Instruction_Register_q),
    .AlwaysQ(PCH));  // open: C
  Register8 GP_Register1 (
    .D(Instruction_Register_q), .Load(decoder_1_out11), .Enable(decoder_2_out11), .Clk(clock_1_out),
    .Reset(Reset), .Q(Instruction_Register_q), .AlwaysQ(GP1));
  Register8 GP_Register2 (
    .D(Instruction_Register_q), .Load(decoder_1_out12), .Enable(decoder_2_out12), .Clk(clock_1_out),
    .Reset(Reset), .Q(Instruction_Register_q), .AlwaysQ(GP2));
  Register8 GP_Register3 (
    .D(Instruction_Register_q), .Load(decoder_1_out13), .Enable(decoder_2_out13), .Clk(clock_1_out),
    .Reset(Reset), .Q(Instruction_Register_q), .AlwaysQ(GP3));
  Register8 GP_Register4 (
    .D(Instruction_Register_q), .Load(decoder_1_out14), .Enable(decoder_2_out14), .Clk(clock_1_out),
    .Reset(Reset), .Q(Instruction_Register_q), .AlwaysQ(GP4));
  Hex_Digit_Display #(.decimalPoint("false")) hex_digit_display_10 (.value(ABH[3:0]));
  Hex_Digit_Display #(.decimalPoint("false")) hex_digit_display_11 (.value(ABL[7:4]));
  Hex_Digit_Display #(.decimalPoint("false")) hex_digit_display_12 (.value(O[7:4]));
  Hex_Digit_Display #(.decimalPoint("false")) hex_digit_display_13 (.value(O[3:0]));
  Hex_Digit_Display #(.decimalPoint("false")) hex_digit_display_14 (.value(Y[7:4]));
  Hex_Digit_Display #(.decimalPoint("false")) hex_digit_display_15 (.value(GP3[7:4]));
  Hex_Digit_Display #(.decimalPoint("false")) hex_digit_display_16 (.value(ABL[3:0]));
  Hex_Digit_Display #(.decimalPoint("false")) hex_digit_display_17 (.value(Y[3:0]));
  Hex_Digit_Display #(.decimalPoint("false")) hex_digit_display_18 (.value(GP3[3:0]));
  Hex_Digit_Display #(.decimalPoint("false")) hex_digit_display_19 (.value(SP[7:4]));
  Hex_Digit_Display #(.decimalPoint("false")) hex_digit_display_20 (.value(SP[3:0]));
  Hex_Digit_Display #(.decimalPoint("false")) hex_digit_display_21 (.value(A[7:4]));
  Hex_Digit_Display #(.decimalPoint("false")) hex_digit_display_22 (.value(A[3:0]));
  Hex_Digit_Display #(.decimalPoint("false")) hex_digit_display_23 (.value(GP0[7:4]));
  Hex_Digit_Display #(.decimalPoint("false")) hex_digit_display_24 (.value(GP0[3:0]));
  Hex_Digit_Display #(.decimalPoint("false")) hex_digit_display_25 (.value(GP4[7:4]));
  Hex_Digit_Display #(.decimalPoint("false")) hex_digit_display_26 (.value(GP4[3:0]));
  Register8 GP_Register0 (
    .D(Instruction_Register_q), .Load(decoder_1_out3), .Enable(decoder_2_out3), .Clk(clock_1_out),
    .Reset(Reset), .Q(Instruction_Register_q), .AlwaysQ(GP0));
  DataLatch8 ALU_out (
    .D(ALU_y), .Load(Microcode_data[4]), .Enable(decoder_2_out5), .Clk(clock_1_out),
    .Q(Instruction_Register_q), .AlwaysQ(O));
  ArithmeticLogicUnit ALU (
    .Opcode(Microcode_data[7:5]), .Cin(S[3]), .A(A), .B(B), .Ignore_Cin(Microcode_data[3]), .Y(ALU_y),
    .C(ALU_n[3]), .Z(ALU_n[2]), .O(ALU_n[1]), .N(ALU_n[0]));
  Register8 Accumulator (
    .D(Instruction_Register_q), .Load(decoder_1_out6), .Enable(decoder_2_out6), .Clk(clock_1_out),
    .Reset(Reset), .Q(Instruction_Register_q), .AlwaysQ(A));
  Register8 Y_Index (
    .D(Instruction_Register_q), .Load(decoder_1_out10), .Enable(decoder_2_out10), .Clk(clock_1_out),
    .Reset(Reset), .Q(Instruction_Register_q), .AlwaysQ(Y));
  Hex_Digit_Display #(.decimalPoint("false")) hex_digit_display_27 (.value(IR[7:4]));
  Hex_Digit_Display #(.decimalPoint("false")) hex_digit_display_28 (.value(IR[3:0]));
  Hex_Digit_Display #(.decimalPoint("false")) hex_digit_display_29 (.value(B[7:4]));
  Hex_Digit_Display #(.decimalPoint("false")) hex_digit_display_30 (.value(B[3:0]));
  Hex_Digit_Display #(.decimalPoint("false")) hex_digit_display_31 (.value(GP1[7:4]));
  Hex_Digit_Display #(.decimalPoint("false")) hex_digit_display_32 (.value(GP1[3:0]));
  Hex_Digit_Display #(.decimalPoint("false")) hex_digit_display_33 (.value(SC));
  StackRegister8 Stack_Pointer (
    .D(Instruction_Register_q), .Load(decoder_1_out8), .Enable(decoder_2_out8), .Clk(clock_1_out),
    .Reset(Reset), .Q(Instruction_Register_q), .AlwaysQ(SP));
  Register4 Status (
    .D(multiplexer_4_out), .Load(Microcode_data[4]), .Enable(decoder_2_out4), .Clk(clock_1_out),
    .Reset(Reset), .Q(Instruction_Register_q[3:0]), .AlwaysQ(S));
  Register8 ALU_B (
    .D(Instruction_Register_q), .Load(decoder_1_out7), .Enable(decoder_2_out7), .Clk(clock_1_out),
    .Reset(Reset), .Q(Instruction_Register_q), .AlwaysQ(B));
  Register8 X_Index (
    .D(Instruction_Register_q), .Load(decoder_1_out9), .Enable(decoder_2_out9), .Clk(clock_1_out),
    .Reset(Reset), .Q(Instruction_Register_q), .AlwaysQ(X));
  ROM #(.addrWidth(14)) rom_1 (.addr({ABH[5:0], ABL}), .data(rom_1_data));
  Multiplexer #(.width(4)) multiplexer_4 (
    .in0(ALU_n), .in1(Instruction_Register_q[3:0]), .out(multiplexer_4_out), .sel(decoder_1_out4));
  and and_5 (and_5_out, ABH[6], ABH[7]);
  and and_6 (and_6_out, and_5_out, decoder_2_out15);
  assign Instruction_Register_q = and_6_out ? rom_1_data : 8'bz;  // Controlled_Buffer controlled_buffer_9
  Multiplexer #(.width(8)) multiplexer_5 (
    .in0({{7{1'b0}}, Microcode_data_2[0]}), .in1(Instruction_Register_q), .out(multiplexer_5_out),
    .sel(decoder_3_out3));
  Multiplexer #(.width(8)) multiplexer_6 (
    .in0(multiplexer_5_out), .in1({8{1'b0}}), .out(multiplexer_6_out), .sel(decoder_1_out5));
  Address_Bus u_ABL (
    .Address(Instruction_Register_q), .Load(demultiplexer_3_out0), .Clk(clock_1_out), .Reset(Reset),
    .Cin(1'b0), .Inc(multiplexer_6_out), .O(ABL), .Cout(ABL_cout));
  Address_Bus u_ABH (
    .Address(Instruction_Register_q), .Load(demultiplexer_3_out1), .Clk(clock_1_out), .Reset(Reset),
    .Cin(ABL_cout), .Inc({8{1'b0}}), .O(ABH));  // open: Cout

  // Notes on the sheet:
  //   contents of Microcode (hex, n*v repeats v):
  //   100 108 f201 2 12*0 100 108 f201 f603 12*0 100 108 f201 f701 f108 7101 6f02 9*0 100 108 f201 f701
  //   f008 7002 10*0 100 108 f201 f700 5613 11*0 100 108 f201 f700 5673 11*0 100 108 f201 f700 56b3 11*0
  //   100 108 f201 f700 5693 11*0 100 108 f201 f700 5653 11*0 100 108 f201 f903 12*0 100 108 f201 fa03
  //   12*0 100 108 f201 6902 12*0 100 108 f201 6a02 12*0 100 108 f201 f701 f108 7100 9f00 7703 8*0 100 108
  //   f201 f701 f108 7100 af00 7703 8*0 100 108 f201 8902 12*0 100 108 f201 9602 12*0 100 108 f201 9802
  //   12*0 100 108 f201 a602 12*0 100 108 f201 f700 5633 11*0 100 108 f201 8100 1108 6f00 8600 1700 583a
  //   7*0 100 108 f201 8600 1700 5818 8100 1108 f602 7*0 100 108 f201 8100 1108 f08 8600 1700 5838 8100 0
  //   f00 8638 583a 0 0 100 108 f201 2700 4600 5472 26*0 100 108 f201 f701 f108 7100 f603 9*0 100 108 f201
  //   f701 f108 7100 f701 0 5612 7*0 100 108 f201 8600 1708 5818 8100 1108 f000 8608 5819 f009 7703 0 0 0
  //   100 108 f201 f701 f108 7100 f701 0 5632 7*0 100 108 f201 2700 4600 5472 10*0 100 108 f201 2204 f001
  //   f00a 10*0 100 108 f201 2224 f001 f00a 10*0 100 108 f201 2244 f001 f00a 10*0 100 108 f201 2264 f001
  //   f00a 10*0 100 108 f201 2284 f001 f00a 10*0 100 108 f201 22a4 f001 f00a 10*0 100 108 f201 22c4 f001
  //   f00a 10*0 100 108 f201 22e4 f001 f00a 10*0 100 108 f201 9600 1700 591a 10*0 100 108 f201 a600 1700
  //   5a1a 10*0 100 108 f201 2700 4600 54b2 10*0 100 108 f201 9600 1700 593a 10*0 100 108 f201 a600 1700
  //   5a3a 10*0 100 108 f201 f700 3b 11*0 100 108 f201 56da 12*0 100 108 f201 56fa 12*0 100 108 f201 56d2
  //   12*0 100 108 f201 56f2 12*0 100 108 f201 f701 f108 7100 f600 56d8 6f00 7703 6*0 100 108 f201 f701
  //   f108 7100 f600 56f8 6f00 7703 6*0 100 108 f201 f701 f108 7100 f600 56d0 6f00 7703 6*0 100 108 f201
  //   f701 f108 7100 f600 56f0 6f00 7703 6*0 100 108 f201 f700 9600 3b 10*0 100 108 f201 f700 a600 3b 10*0
  //   100 108 f201 f701 f108 7100 f701 9600 3a 7*0 100 108 f201 f701 f108 7100 f701 a600 3a 7*0 100 108
  //   f201 f701 f108 7100 f903 9*0 100 108 f201 f701 f108 7100 fa03 9*0 100 108 f201 f701 f108 7100 9906
  //   f603 8*0 100 108 f201 f701 f108 7100 aa06 f603 8*0 100 108 f201 f701 f108 7100 9906 f701 5672 7*0
  //   100 108 f201 f701 f108 7100 aa06 f701 5672 7*0 100 108 f201 f701 f108 7100 9907 0 6f02 7*0 100 108
  //   f201 f701 f108 7100 aa07 0 6f02 7*0 100 108 f201 1700 561a 11*0 100 108 f201 f701 f108 7100 f600
  //   1700 5f18 3 6*0 100 108 f201 f701 f108 7100 f701 f108 7100 6f00 3 5*0 100 108 f201 f701 f108 7100
  //   9906 f701 5612 7*0 100 108 f201 f701 f108 7100 aa06 f701 5612 7*0 100 108 f201 f700 561b 11*0 100
  //   108 f201 f700 563b 11*0 100 108 f201 f701 f108 7100 f701 0 561a 7*0 100 108 f201 f701 f108 7100 f701
  //   0 563a 7*0 100 108 f201 f303 12*0 100 108 f201 fb03 12*0 100 108 f201 fc03 12*0 100 108 f201 fd03
  //   12*0 100 108 f201 fe03 12*0 100 108 f201 f701 f108 7100 f303 9*0 100 108 f201 f701 f108 7100 fb03
  //   9*0 100 108 f201 f701 f108 7100 fc03 9*0 100 108 f201 f701 f108 7100 fd03 9*0 100 108 f201 f701 f108
  //   7100 fe03 9*0 100 108 f201 6302 12*0 100 108 f201 6b02 12*0 100 108 f201 6c02 12*0 100 108 f201 6d02
  //   12*0 100 108 f201 6e02 12*0 100 108 f201 3602 12*0 100 108 f201 b602 12*0 100 108 f201 c602 12*0 100
  //   108 f201 d602 12*0 100 108 f201 e602 12*0 100 108 f201 9302 12*0 100 108 f201 9b02 12*0 100 108 f201
  //   9c02 12*0 100 108 f201 9d02 12*0 100 108 f201 9e02 12*0 100 108 f201 3902 12*0 100 108 f201 b902
  //   12*0 100 108 f201 c902 12*0 100 108 f201 d902 12*0 100 108 f201 e902 12*0 100 108 f201 a302 12*0 100
  //   108 f201 ab02 12*0 100 108 f201 ac02 12*0 100 108 f201 ad02 12*0 100 108 f201 ae02 12*0 100 108 f201
  //   3a02 12*0 100 108 f201 ba02 12*0 100 108 f201 ca02 12*0 100 108 f201 da02 12*0 100 108 f201 ea02
  //   12*0 100 108 f201 f701 f108 7100 f701 f108 7100 f602
  //   C
  //   Z
  //   Program Counter
  //   Status
  //   O
  //   N
  //   X Index
  //   General Purpose 2
  //   Address Bus
  //   ALU Out
  //   Y Index
  //   General Purpose 3
  //   Stack Pointer
  //   Accumulator
  //   General Purpose 0
  //   General Purpose 4
  //   Instruction
  //   ALU B
  //   General Purpose 1
  //   Step Counter
  //   contents of rom_1 (hex, n*v repeats v):
  //   15*ff e1 2 ed 3 8d 3 e4 f 89 4 e2 13 86 5 e1 15 84 6 e0 17 82 7 df 18 82 8 de 22 dd 24 dc 24 dc 25
  //   db 25 da 27 d9 28 d8 28 d8 26 da 23 dd 23 dd 23 dd 23 dd 23 dd 23 dd 1d 82 4 dd 1e 83 2 dc 20 de 23
  //   dc 24 dc 24 db 25 dc 22 81 1 dc 22 df 21 e0 1f e4 1b e6 1a e6 1b e5 1b e5 1c e4 1d e2 1c e4 1c e5 1c
  //   e4 18 81 1 81 1 e4 1 81 16 ea 1 81 13 ca 1 a2 f 81 1 81 1 c9 2 a3 2 81 a 82 1 ca 3 a7 9 cd 3 a7 9 cc
  //   5 a4 d a9 1 9f 7 9f 14 a6 2 9e 9 9a 1b a2 2 9d b 98 1d a0 4 9b d 96 1f 9d 6 9a f 95 20 9a 9 98 11 93
  //   21 98 b 97 13 92 21 97 d 95 14 91 23 95 f 93 16 90 23 94 10 92 18 8e 24 93 12 90 1a 8d 25 90 14 8f
  //   1c 8c 25 8f 16 8d 1e 8b 25 8d 19 8b 21 88 2c 85 1b 89 29 82 4d 87 7a 85 7c 84 7d 83 7d 83 d 82 4 81
  //   6a 82 c 84 2 83 6a 81 c 84 2 84 3b 82 38 86 1 85 3b 83 2b 83 7 8e 14 82 25 83 1c 82 c 85 5 8e 4 85 a
  //   84 23 85 15 84 2 83 b 86 3 8f 2 88 8 85 22 87 8 84 6 86 1 85 a 87 1 9b 6 87 21 89 5 87 3 87 1 85 a
  //   a3 5 88 21 8a 3 89 2 8d a a4 3 89 21 8b 1 9a 9 a5 1 8a 21 a6 9 b0 21 a7 4 b4 21 df 21 df 21 df 21 df
  //   21 df 21 df 21 df 21 df 21 e0 1f e5 1a e6 17 ea 16 ea 16 ea 17 e9 17 e8 18 e7 1a e5 1c e4 1d e4 1b
  //   e5 1b e5 1b e5 1a e6 1a e7 1a e6 1a e5 1c e4 1c e4 1c e3 1e e2 1e af
endmodule

module ArithmeticLogicUnit (
  input  [2:0] Opcode,
  input  Cin,
  input  [7:0] A,
  input  [7:0] B,
  input  Ignore_Cin,
  output [7:0] Y,
  output C,
  output Z,
  output O,
  output N
);

  wire and_1_out, and_2_out, and_3_out, and_4_out, and_5_out, and_6_out, cla8_1_c0, multiplexer_2_out,
       multiplexer_3_out, multiplexer_4_out, not_1_out, not_2_out, not_3_out, not_4_out, not_5_out,
       not_6_out, not_7_out, not_8_out, not_9_out, not_10_out, not_11_out, not_12_out, not_13_out, xor_1_out,
       xor_2_out;
  wire [0:0] multiplexer_1_out;
  wire [7:0] and_8_out, cla8_1_sum, multiplexer_5_out, negate8_1_nega, not_14_out, or_2_out, xor_3_out;

  not not_1 (not_1_out, Opcode[0]);
  and and_1 (and_1_out, not_1_out, Opcode[1], Opcode[2]);
  and and_2 (and_2_out, and_1_out, A[7]);
  and and_3 (and_3_out, Opcode[0], Opcode[1], Opcode[2]);
  // Probe on A
  // Probe on A
  // Probe on A
  // Probe on B
  // Probe on B
  // Probe on B
  not not_2 (not_2_out, Opcode[1]);
  not not_3 (not_3_out, Opcode[2]);
  and and_4 (and_4_out, not_2_out, not_3_out);
  and and_5 (and_5_out, and_3_out, A[0]);
  and and_6 (and_6_out, and_4_out, cla8_1_c0);
  or or_1 (C, and_2_out, and_5_out, and_6_out);
  xor xor_1 (xor_1_out, A[7], B[7]);
  not not_4 (not_4_out, N);
  not not_5 (not_5_out, Y[6]);
  not not_6 (not_6_out, Y[5]);
  not not_7 (not_7_out, Y[4]);
  and and_7 (Z, not_4_out, not_5_out, not_6_out, not_7_out, not_9_out, not_10_out, not_11_out, not_12_out);
  Multiplexer multiplexer_1 (.in0(Cin), .in1(1'b0), .out(multiplexer_1_out[0]), .sel(Ignore_Cin));
  not not_8 (not_8_out, xor_1_out);
  Multiplexer multiplexer_2 (.in0(not_8_out), .in1(xor_1_out), .out(multiplexer_2_out), .sel(Opcode[0]));
  not not_9 (not_9_out, Y[3]);
  not not_10 (not_10_out, Y[2]);
  not not_11 (not_11_out, Y[1]);
  not not_12 (not_12_out, Y[0]);
  and and_8 (and_8_out[0], A[0], B[0]);
  and and_9 (and_8_out[1], A[1], B[1]);
  and and_10 (and_8_out[2], A[2], B[2]);
  and and_11 (and_8_out[3], A[3], B[3]);
  and and_12 (and_8_out[4], A[4], B[4]);
  and and_13 (and_8_out[5], A[5], B[5]);
  and and_14 (and_8_out[6], A[6], B[6]);
  and and_15 (and_8_out[7], A[7], B[7]);
  or or_2 (or_2_out[0], A[0], B[0]);
  or or_3 (or_2_out[1], A[1], B[1]);
  or or_4 (or_2_out[2], A[2], B[2]);
  or or_5 (or_2_out[3], A[3], B[3]);
  or or_6 (or_2_out[4], A[4], B[4]);
  or or_7 (or_2_out[5], A[5], B[5]);
  or or_8 (or_2_out[6], A[6], B[6]);
  or or_9 (or_2_out[7], A[7], B[7]);
  xor xor_2 (xor_2_out, A[7], N);
  and and_16 (O, multiplexer_2_out, xor_2_out);
  Negate8 negate8_1 (.A(B), .NegA(negate8_1_nega));
  Multiplexer multiplexer_3 (.in0(Cin), .in1(not_13_out), .out(multiplexer_3_out), .sel(Opcode[0]));
  not not_13 (not_13_out, Cin);
  Multiplexer multiplexer_4 (.in0(multiplexer_3_out), .in1(1'b0), .out(multiplexer_4_out), .sel(Ignore_Cin));
  Multiplexer #(.width(8)) multiplexer_5 (.in0(B), .in1(negate8_1_nega), .out(multiplexer_5_out), .sel(Opcode[0]));
  not not_14 (not_14_out[0], A[0]);
  not not_15 (not_14_out[1], A[1]);
  not not_16 (not_14_out[2], A[2]);
  not not_17 (not_14_out[3], A[3]);
  not not_18 (not_14_out[4], A[4]);
  not not_19 (not_14_out[5], A[5]);
  not not_20 (not_14_out[6], A[6]);
  not not_21 (not_14_out[7], A[7]);
  xor xor_3 (xor_3_out[0], A[0], B[0]);
  xor xor_4 (xor_3_out[1], A[1], B[1]);
  xor xor_5 (xor_3_out[2], A[2], B[2]);
  xor xor_6 (xor_3_out[3], A[3], B[3]);
  xor xor_7 (xor_3_out[4], A[4], B[4]);
  xor xor_8 (xor_3_out[5], A[5], B[5]);
  xor xor_9 (xor_3_out[6], A[6], B[6]);
  xor xor_10 (xor_3_out[7], A[7], B[7]);
  CLA8 cla8_1 (.A(A), .B(multiplexer_5_out), .Cin(multiplexer_4_out), .C0(cla8_1_c0), .Sum(cla8_1_sum));
  Multiplexer #(.select(3), .width(8)) multiplexer_6 (
    .in0(cla8_1_sum), .in1(cla8_1_sum), .in2(not_14_out), .in3(and_8_out), .in4(xor_3_out), .in5(or_2_out),
    .in6({A[6:0], multiplexer_1_out[0]}), .in7({multiplexer_1_out[0], A[7:1]}), .out({N, Y[6:0]}),
    .sel(Opcode));
  // Probe on {N, Y[6:0]}
  // Probe on {N, Y[6:0]}
  // Probe on {N, Y[6:0]}

  assign Y[7] = N;

  // Notes on the sheet:
  //   Status Flags
endmodule

module ProgramCounter (
  input  Cin,
  input  [1:0] Inc,
  input  Load,
  input  Reset,
  input  Clk,
  input  [7:0] Address,
  input  Enable,
  output C,
  output [7:0] PC,
  output [7:0] AlwaysQ
);

  wire [7:0] cla8_1_sum, multiplexer_1_out, register8_1_q;

  CLA8 cla8_1 (.A(register8_1_q), .B({{6{1'b0}}, Inc}), .Cin(Cin), .C0(C), .Sum(cla8_1_sum));
  Multiplexer #(.width(8)) multiplexer_1 (.in0(cla8_1_sum), .in1(Address), .out(multiplexer_1_out), .sel(Load));
  Register8 register8_1 (
    .D(multiplexer_1_out), .Load(1'b1), .Enable(1'b1), .Clk(Clk), .Reset(Reset), .Q(register8_1_q),
    .AlwaysQ(AlwaysQ));
  assign PC = Enable ? register8_1_q : 8'bz;  // Controlled_Buffer controlled_buffer_1
endmodule

module Address_Bus (
  input  [7:0] Address,
  input  Load,
  input  Clk,
  input  Reset,
  input  Cin,
  input  [7:0] Inc,
  output [7:0] O,
  output Cout
);

  wire [7:0] cla8_1_sum, multiplexer_1_out;

  Multiplexer #(.width(8)) multiplexer_1 (.in0(cla8_1_sum), .in1(Address), .out(multiplexer_1_out), .sel(Load));
  CLA8 cla8_1 (.A(O), .B(Inc), .Cin(Cin), .C0(Cout), .Sum(cla8_1_sum));
  Register8 register8_1 (
    .D(multiplexer_1_out), .Load(1'b1), .Enable(1'b1), .Clk(Clk), .Reset(Reset), .Q(O));  // open: AlwaysQ
endmodule

module Increment8 (
  input  Reset,
  input  Clk,
  input  Cin,
  input  Inc,
  output [7:0] O
);

  wire [7:0] cla8_1_sum;

  CLA8 cla8_1 (.A(O), .B({{7{1'b0}}, Inc}), .Cin(Cin), .Sum(cla8_1_sum));  // open: C0
  Register8 register8_1 (.D(cla8_1_sum), .Load(1'b1), .Enable(1'b1), .Clk(Clk), .Reset(Reset), .Q(O));  // open: AlwaysQ
endmodule

module Increment4 (
  input  Reset,
  input  Clk,
  output [3:0] O
);

  wire d_flipflop_1_q, undriven;
  wire [3:0] cla4_1_sum;

  D_FlipFlop d_flipflop_1 (.D(Reset), .Clk(Clk), .Reset(undriven), .Q(d_flipflop_1_q));  // open: Qbar
  CLA4 cla4_1 (.A(O), .B(4'b0001), .Sum(cla4_1_sum));  // open: Cin, Cout, PG, GG
  D_FlipFlop d_flipflop_2 (.D(cla4_1_sum[0]), .Clk(Clk), .Reset(d_flipflop_1_q), .Q(O[0]));  // open: Qbar
  D_FlipFlop d_flipflop_3 (.D(cla4_1_sum[1]), .Clk(Clk), .Reset(d_flipflop_1_q), .Q(O[1]));  // open: Qbar
  D_FlipFlop d_flipflop_4 (.D(cla4_1_sum[2]), .Clk(Clk), .Reset(d_flipflop_1_q), .Q(O[2]));  // open: Qbar
  D_FlipFlop d_flipflop_5 (.D(cla4_1_sum[3]), .Clk(Clk), .Reset(d_flipflop_1_q), .Q(O[3]));  // open: Qbar
endmodule

module Register8 (
  input  [7:0] D,
  input  Load,
  input  Enable,
  input  Clk,
  input  Reset,
  output [7:0] Q,
  output [7:0] AlwaysQ
);

  wire multiplexer_1_out, multiplexer_2_out, multiplexer_3_out, multiplexer_4_out, multiplexer_5_out,
       multiplexer_6_out, multiplexer_7_out, multiplexer_8_out;

  Multiplexer multiplexer_1 (.in0(AlwaysQ[0]), .in1(D[0]), .out(multiplexer_1_out), .sel(Load));
  Multiplexer multiplexer_2 (.in0(AlwaysQ[1]), .in1(D[1]), .out(multiplexer_2_out), .sel(Load));
  Multiplexer multiplexer_3 (.in0(AlwaysQ[2]), .in1(D[2]), .out(multiplexer_3_out), .sel(Load));
  Multiplexer multiplexer_4 (.in0(AlwaysQ[3]), .in1(D[3]), .out(multiplexer_4_out), .sel(Load));
  Multiplexer multiplexer_5 (.in0(AlwaysQ[4]), .in1(D[4]), .out(multiplexer_5_out), .sel(Load));
  Multiplexer multiplexer_6 (.in0(AlwaysQ[5]), .in1(D[5]), .out(multiplexer_6_out), .sel(Load));
  Multiplexer multiplexer_7 (.in0(AlwaysQ[6]), .in1(D[6]), .out(multiplexer_7_out), .sel(Load));
  Multiplexer multiplexer_8 (.in0(AlwaysQ[7]), .in1(D[7]), .out(multiplexer_8_out), .sel(Load));
  D_FlipFlop d_flipflop_1 (.D(multiplexer_1_out), .Clk(Clk), .Reset(Reset), .Q(AlwaysQ[0]));  // open: Qbar
  D_FlipFlop d_flipflop_2 (.D(multiplexer_2_out), .Clk(Clk), .Reset(Reset), .Q(AlwaysQ[1]));  // open: Qbar
  D_FlipFlop d_flipflop_3 (.D(multiplexer_3_out), .Clk(Clk), .Reset(Reset), .Q(AlwaysQ[2]));  // open: Qbar
  D_FlipFlop d_flipflop_4 (.D(multiplexer_4_out), .Clk(Clk), .Reset(Reset), .Q(AlwaysQ[3]));  // open: Qbar
  D_FlipFlop d_flipflop_5 (.D(multiplexer_5_out), .Clk(Clk), .Reset(Reset), .Q(AlwaysQ[4]));  // open: Qbar
  D_FlipFlop d_flipflop_6 (.D(multiplexer_6_out), .Clk(Clk), .Reset(Reset), .Q(AlwaysQ[5]));  // open: Qbar
  D_FlipFlop d_flipflop_7 (.D(multiplexer_7_out), .Clk(Clk), .Reset(Reset), .Q(AlwaysQ[6]));  // open: Qbar
  D_FlipFlop d_flipflop_8 (.D(multiplexer_8_out), .Clk(Clk), .Reset(Reset), .Q(AlwaysQ[7]));  // open: Qbar
  assign Q = Enable ? AlwaysQ : 8'bz;  // Controlled_Buffer controlled_buffer_1
endmodule

module DataLatch8 (
  input  [7:0] D,
  input  Load,
  input  Enable,
  input  Clk,
  output [7:0] Q,
  output [7:0] AlwaysQ
);

  wire and_1_out, not_1_out;

  and and_1 (and_1_out, Load, not_1_out);
  not not_1 (not_1_out, Clk);
  D_Latch d_latch_1 (.D(D[0]), .Enable(and_1_out), .Q(AlwaysQ[0]));  // open: Qbar
  D_Latch d_latch_2 (.D(D[1]), .Enable(and_1_out), .Q(AlwaysQ[1]));  // open: Qbar
  D_Latch d_latch_3 (.D(D[2]), .Enable(and_1_out), .Q(AlwaysQ[2]));  // open: Qbar
  D_Latch d_latch_4 (.D(D[3]), .Enable(and_1_out), .Q(AlwaysQ[3]));  // open: Qbar
  D_Latch d_latch_5 (.D(D[4]), .Enable(and_1_out), .Q(AlwaysQ[4]));  // open: Qbar
  D_Latch d_latch_6 (.D(D[5]), .Enable(and_1_out), .Q(AlwaysQ[5]));  // open: Qbar
  D_Latch d_latch_7 (.D(D[6]), .Enable(and_1_out), .Q(AlwaysQ[6]));  // open: Qbar
  D_Latch d_latch_8 (.D(D[7]), .Enable(and_1_out), .Q(AlwaysQ[7]));  // open: Qbar
  assign Q = Enable ? AlwaysQ : 8'bz;  // Controlled_Buffer controlled_buffer_1
endmodule

module Register4 (
  input  [3:0] D,
  input  Load,
  input  Enable,
  input  Clk,
  input  Reset,
  output [3:0] Q,
  output [3:0] AlwaysQ
);

  wire multiplexer_1_out, multiplexer_2_out, multiplexer_3_out, multiplexer_4_out;

  Multiplexer multiplexer_1 (.in0(AlwaysQ[0]), .in1(D[0]), .out(multiplexer_1_out), .sel(Load));
  Multiplexer multiplexer_2 (.in0(AlwaysQ[1]), .in1(D[1]), .out(multiplexer_2_out), .sel(Load));
  Multiplexer multiplexer_3 (.in0(AlwaysQ[2]), .in1(D[2]), .out(multiplexer_3_out), .sel(Load));
  Multiplexer multiplexer_4 (.in0(AlwaysQ[3]), .in1(D[3]), .out(multiplexer_4_out), .sel(Load));
  D_FlipFlop d_flipflop_1 (.D(multiplexer_1_out), .Clk(Clk), .Reset(Reset), .Q(AlwaysQ[0]));  // open: Qbar
  D_FlipFlop d_flipflop_2 (.D(multiplexer_2_out), .Clk(Clk), .Reset(Reset), .Q(AlwaysQ[1]));  // open: Qbar
  D_FlipFlop d_flipflop_3 (.D(multiplexer_3_out), .Clk(Clk), .Reset(Reset), .Q(AlwaysQ[2]));  // open: Qbar
  D_FlipFlop d_flipflop_4 (.D(multiplexer_4_out), .Clk(Clk), .Reset(Reset), .Q(AlwaysQ[3]));  // open: Qbar
  assign Q = Enable ? AlwaysQ : 4'bz;  // Controlled_Buffer controlled_buffer_1
endmodule

module StackRegister8 (
  input  [7:0] D,
  input  Load,
  input  Enable,
  input  Clk,
  input  Reset,
  output [7:0] Q,
  output [7:0] AlwaysQ
);

  wire multiplexer_1_out, multiplexer_2_out, multiplexer_3_out, multiplexer_4_out, multiplexer_5_out,
       multiplexer_6_out, multiplexer_7_out, multiplexer_8_out, multiplexer_9_out, multiplexer_10_out,
       multiplexer_11_out, multiplexer_12_out, multiplexer_13_out, multiplexer_14_out, multiplexer_15_out,
       multiplexer_16_out;

  Multiplexer multiplexer_1 (.in0(AlwaysQ[0]), .in1(D[0]), .out(multiplexer_1_out), .sel(Load));
  Multiplexer multiplexer_2 (.in0(AlwaysQ[1]), .in1(D[1]), .out(multiplexer_2_out), .sel(Load));
  Multiplexer multiplexer_3 (.in0(AlwaysQ[2]), .in1(D[2]), .out(multiplexer_3_out), .sel(Load));
  Multiplexer multiplexer_4 (.in0(AlwaysQ[3]), .in1(D[3]), .out(multiplexer_4_out), .sel(Load));
  Multiplexer multiplexer_5 (.in0(AlwaysQ[4]), .in1(D[4]), .out(multiplexer_5_out), .sel(Load));
  Multiplexer multiplexer_6 (.in0(AlwaysQ[5]), .in1(D[5]), .out(multiplexer_6_out), .sel(Load));
  Multiplexer multiplexer_7 (.in0(AlwaysQ[6]), .in1(D[6]), .out(multiplexer_7_out), .sel(Load));
  Multiplexer multiplexer_8 (.in0(AlwaysQ[7]), .in1(D[7]), .out(multiplexer_8_out), .sel(Load));
  Multiplexer multiplexer_9 (.in0(multiplexer_1_out), .in1(1'b1), .out(multiplexer_9_out), .sel(Reset));
  Multiplexer multiplexer_10 (.in0(multiplexer_2_out), .in1(1'b1), .out(multiplexer_10_out), .sel(Reset));
  Multiplexer multiplexer_11 (.in0(multiplexer_3_out), .in1(1'b1), .out(multiplexer_11_out), .sel(Reset));
  Multiplexer multiplexer_12 (.in0(multiplexer_4_out), .in1(1'b1), .out(multiplexer_12_out), .sel(Reset));
  Multiplexer multiplexer_13 (.in0(multiplexer_5_out), .in1(1'b1), .out(multiplexer_13_out), .sel(Reset));
  Multiplexer multiplexer_14 (.in0(multiplexer_6_out), .in1(1'b1), .out(multiplexer_14_out), .sel(Reset));
  Multiplexer multiplexer_15 (.in0(multiplexer_7_out), .in1(1'b1), .out(multiplexer_15_out), .sel(Reset));
  Multiplexer multiplexer_16 (.in0(multiplexer_8_out), .in1(1'b1), .out(multiplexer_16_out), .sel(Reset));
  D_FlipFlop d_flipflop_1 (.D(multiplexer_9_out), .Clk(Clk), .Q(AlwaysQ[0]));  // open: Reset, Qbar
  D_FlipFlop d_flipflop_2 (.D(multiplexer_10_out), .Clk(Clk), .Q(AlwaysQ[1]));  // open: Reset, Qbar
  D_FlipFlop d_flipflop_3 (.D(multiplexer_11_out), .Clk(Clk), .Q(AlwaysQ[2]));  // open: Reset, Qbar
  D_FlipFlop d_flipflop_4 (.D(multiplexer_12_out), .Clk(Clk), .Q(AlwaysQ[3]));  // open: Reset, Qbar
  D_FlipFlop d_flipflop_5 (.D(multiplexer_13_out), .Clk(Clk), .Q(AlwaysQ[4]));  // open: Reset, Qbar
  D_FlipFlop d_flipflop_6 (.D(multiplexer_14_out), .Clk(Clk), .Q(AlwaysQ[5]));  // open: Reset, Qbar
  D_FlipFlop d_flipflop_7 (.D(multiplexer_15_out), .Clk(Clk), .Q(AlwaysQ[6]));  // open: Reset, Qbar
  D_FlipFlop d_flipflop_8 (.D(multiplexer_16_out), .Clk(Clk), .Q(AlwaysQ[7]));  // open: Reset, Qbar
  assign Q = Enable ? AlwaysQ : 8'bz;  // Controlled_Buffer controlled_buffer_1
endmodule

module Negate8 (
  input  [7:0] A,
  output [7:0] NegA
);

  wire [7:0] not_1_out;

  // Probe on A
  not not_1 (not_1_out[0], A[0]);
  not not_2 (not_1_out[1], A[1]);
  not not_3 (not_1_out[2], A[2]);
  not not_4 (not_1_out[3], A[3]);
  not not_5 (not_1_out[4], A[4]);
  not not_6 (not_1_out[5], A[5]);
  not not_7 (not_1_out[6], A[6]);
  not not_8 (not_1_out[7], A[7]);
  CLA8 cla8_1 (.A(not_1_out), .B(8'h1), .Sum(NegA));  // open: Cin, C0
  // Probe on NegA
endmodule

module CLA8 (
  input  [7:0] A,
  input  [7:0] B,
  input  Cin,
  output C0,
  output [7:0] Sum
);

  wire cla4_1_gg, cla4_1_pg, cla4_2_gg, cla4_2_pg, lcu2_1_c1;

  // Probe on A
  // Probe on B
  CLA4 cla4_1 (.A(A[7:4]), .B(B[7:4]), .Cin(lcu2_1_c1), .Sum(Sum[7:4]), .PG(cla4_1_pg), .GG(cla4_1_gg));  // open: Cout
  CLA4 cla4_2 (.A(A[3:0]), .B(B[3:0]), .Cin(Cin), .Sum(Sum[3:0]), .PG(cla4_2_pg), .GG(cla4_2_gg));  // open: Cout
  LCU2 lcu2_1 (.P1(cla4_1_pg), .G1(cla4_1_gg), .P0(cla4_2_pg), .G0(cla4_2_gg), .C0(Cin), .C2(C0), .C1(lcu2_1_c1));
  // Probe on Sum
endmodule

module CLA4 (
  input  [3:0] A,
  input  [3:0] B,
  input  Cin,
  output Cout,
  output [3:0] Sum,
  output PG,
  output GG
);

  wire partialfulladder_1_g, partialfulladder_1_p, partialfulladder_2_g, partialfulladder_2_p,
       partialfulladder_3_g, partialfulladder_3_p, partialfulladder_4_g, partialfulladder_4_p;

  PartialFullAdder partialfulladder_1 (.A(A[3]), .B(B[3]), .P(partialfulladder_1_p), .G(partialfulladder_1_g));
  PartialFullAdder partialfulladder_2 (.A(A[2]), .B(B[2]), .P(partialfulladder_2_p), .G(partialfulladder_2_g));
  PartialFullAdder partialfulladder_3 (.A(A[1]), .B(B[1]), .P(partialfulladder_3_p), .G(partialfulladder_3_g));
  PartialFullAdder partialfulladder_4 (.A(A[0]), .B(B[0]), .P(partialfulladder_4_p), .G(partialfulladder_4_g));
  CLU4 clu4_1 (
    .P3(partialfulladder_1_p), .G3(partialfulladder_1_g), .P2(partialfulladder_2_p),
    .G2(partialfulladder_2_g), .P1(partialfulladder_3_p), .G1(partialfulladder_3_g),
    .P0(partialfulladder_4_p), .G0(partialfulladder_4_g), .C0(Cin), .PG(PG), .GG(GG), .C4(Cout), .S3(Sum[3]),
    .S2(Sum[2]), .S1(Sum[1]), .S0(Sum[0]));
  // Probe on Sum
endmodule

module PartialFullAdder (
  input  A,
  input  B,
  output P,
  output G
);

  and and_1 (G, A, B);
  xor xor_1 (P, A, B);
endmodule

module CLU4 (
  input  P3,
  input  G3,
  input  P2,
  input  G2,
  input  P1,
  input  G1,
  input  P0,
  input  G0,
  input  C0,
  output PG,
  output GG,
  output C4,
  output S3,
  output S2,
  output S1,
  output S0
);

  wire and_1_out, and_2_out, and_3_out, and_4_out, and_5_out, and_6_out, and_7_out, and_8_out, and_9_out,
       and_10_out, or_1_out, or_2_out, or_3_out;

  and and_1 (and_1_out, P3, P2, P1, P0, C0);
  and and_2 (and_2_out, P3, P2, P1, G0);
  and and_3 (and_3_out, P3, P2, G1);
  and and_4 (and_4_out, G2, P3);
  and and_5 (and_5_out, P2, P1, P0, C0);
  and and_6 (and_6_out, P2, P1, G0);
  and and_7 (and_7_out, G1, P2);
  and and_8 (and_8_out, P1, P0, C0);
  and and_9 (and_9_out, G0, P1);
  and and_10 (and_10_out, C0, P0);
  or or_1 (or_1_out, and_5_out, and_6_out, and_7_out, G2);
  or or_2 (or_2_out, and_8_out, and_9_out, G1);
  or or_3 (or_3_out, and_10_out, G0);
  and and_11 (PG, P3, P2, P1, P0);
  or or_4 (GG, and_2_out, and_3_out, and_4_out, G3);
  or or_5 (C4, and_1_out, and_2_out, and_3_out, and_4_out, G3);
  xor xor_1 (S3, P3, or_1_out);
  xor xor_2 (S2, P2, or_2_out);
  xor xor_3 (S1, P1, or_3_out);
  xor xor_4 (S0, P0, C0);
endmodule

module LCU2 (
  input  P1,
  input  G1,
  input  P0,
  input  G0,
  input  C0,
  output C2,
  output C1
);

  wire and_1_out, and_2_out, and_3_out;

  and and_1 (and_1_out, P1, P0, C0);
  and and_2 (and_2_out, G0, P1);
  and and_3 (and_3_out, C0, P0);
  or or_1 (C2, and_1_out, and_2_out, G1);
  or or_2 (C1, and_3_out, G0);
endmodule

module D_FlipFlop (
  input  D,
  input  Clk,
  input  Reset,
  output Q,
  output Qbar
);

  wire nand_1_out, nand_2_out, nand_3_out, nand_4_out, not_1_out;

  not not_1 (not_1_out, Reset);
  nand nand_1 (nand_1_out, nand_4_out, nand_2_out);
  nand nand_2 (nand_2_out, nand_1_out, Clk, not_1_out);
  nand nand_3 (nand_3_out, nand_2_out, Clk, nand_4_out);
  nand nand_4 (nand_4_out, nand_3_out, D, not_1_out);
  nand nand_5 (Q, nand_2_out, Qbar);
  nand nand_6 (Qbar, Q, nand_3_out, not_1_out);
endmodule

module D_Latch (
  input  D,
  input  Enable,
  output Q,
  output Qbar
);

  wire nand_1_out, nand_2_out, not_1_out;

  not not_1 (not_1_out, D);
  nand nand_1 (nand_1_out, D, Enable);
  nand nand_2 (nand_2_out, Enable, not_1_out);
  nand nand_3 (Q, nand_1_out, Qbar);
  nand nand_4 (Qbar, Q, nand_2_out);
endmodule
